// Logisim project cpu_addi_pipe.circ as structural Verilog: 1 circuit, main circuit main
module main (
  input  [31:0] INSTRUCTION,
  input  CLOCK,
  output [31:0] PROGRAM_COUNTER,
  output [31:0] ra,
  output [31:0] sp,
  output [31:0] t0,
  output [31:0] t1,
  output [31:0] t2,
  output [31:0] s0,
  output [31:0] s1,
  output [31:0] a0
);

  wire [11:0] imm;
  wire [19:0] INSTRUCTION_Q;
  wire [31:0] adder_1_out, alu_result, RegFile_read_data_1;

  // control_logic control_logic_1: pin names not known
  Adder #(.width(32)) adder_1 (.a(PROGRAM_COUNTER), .b(32'h4), .out(adder_1_out));  // open: cin, cout
  Register #(.width(32)) register_1 (.D(INSTRUCTION), .clk(CLOCK), .Q({imm, INSTRUCTION_Q}));  // open: en, clr
  Register #(.width(32)) PC (.D(adder_1_out), .clk(CLOCK), .Q(PROGRAM_COUNTER));  // open: en, clr
  // imm_gen imm_gen_1: pin names not known
  // branch_comp branch_comp_1: pin names not known
  regfile_main RegFile (
    .rd(INSTRUCTION_Q[11:7]), .Read_Data_1(RegFile_read_data_1), .ra(ra), .sp(sp), .t0(t0), .t1(t1), .t2(t2),
    .s0(s0), .s1(s1), .a0(a0), .rs1(INSTRUCTION_Q[19:15]), .Write_Data(alu_result), .RegWEn(1'b1), .clk(CLOCK));  // open: rs2, Read_Data_2
  alu Arithmetic_Logic_Unit (.Result(alu_result), .A(RegFile_read_data_1), .B({{20{1'b0}}, imm}));  // open: ALUSel
  // mem_main DMEM: pin names not known

  // Other names for the same wires on the sheet: INSTRUCTION_Q[31:20] = imm; clk = CLOCK;
  //   rd_Sel[4:0] = INSTRUCTION_Q[11:7]; rs1_Sel[4:0] = INSTRUCTION_Q[19:15]

  // Notes on the sheet:
  //   Output
  //   IMEM (do **NOT** move this)
  //   Inputs
  //   It is OK to move the PC, RegFile, ALU, MEM, Branch Comp, Imm Gen, and Control Logic to wherever is most convenient for you when constructing your CPU, and to delete this text
  //   Inputs/Outputs for testing. Do **NOT** move these.
endmodule
